# Fritzing sketch ControllerShield (saved by Fritzing 0.9.3b)
circuit board: 8.80596cm x 5.59225cm
breadboards: 1

parts:
  VCC = Battery block 9V
  D7 = Momentary Switch [package=ksa_sealed_tac_switch]
  D6 = Momentary Switch [package=ksa_sealed_tac_switch]
  D5 = Momentary Switch [package=ksa_sealed_tac_switch]
  D4 = Momentary Switch [package=ksa_sealed_tac_switch]
  D3 = Momentary Switch [package=ksa_sealed_tac_switch]
  D2 = Momentary Switch [package=ksa_sealed_tac_switch]
  A5 = POT [package=pot_alpha_rv16af-20]
  R1 = Resistor [tolerance=±5% resistance=220 package=THT]
  R2 = Resistor [tolerance=±5% resistance=220 package=THT]
  R3 = Resistor [tolerance=±5% resistance=220 package=THT]
  R4 = Resistor [tolerance=±5% resistance=220 package=THT]
  R5 = Resistor [tolerance=±5% resistance=220 package=THT]
  R6 = Resistor [tolerance=±5% resistance=220 package=THT]
  GND = Arduino Uno (Rev3) - ICSP

nets:
  N1: VCC.-, A5.E, R1.Pin_1, R2.Pin_1, R3.Pin_1, R4.Pin_1, R5.Pin_1, R6.Pin_1, GND.GND
  N2: VCC.+, GND.VIN
  N3: D7.1, GND.D7
  N4: D7.2, R1.Pin_0
  N5: D7.4, D6.4, D5.4, D4.4, D3.4, D2.4, A5.A, GND.5V
  N6: D6.1, GND.D6_PWM
  N7: D6.2, R2.Pin_0
  N8: D5.1, GND.D5_PWM
  N9: D5.2, R3.Pin_0
  N10: D4.1, GND.D4
  N11: D4.2, R4.Pin_0
  N12: D3.1, GND.D3_PWM
  N13: D3.2, R5.Pin_0
  N14: D2.1, GND.D2
  N15: D2.2, R6.Pin_0
  N16: A5.S, GND.A5/SCL
